# Fritzing sketch cf-thermostat-nodemcu (saved by Fritzing 0.8.7b)

parts:
  DHT11_1 = DHT11 module
  U2 = NodeMCU V3.0

nets:
  VCC: DHT11_1.VCC, U2.3V3
  GND: DHT11_1.GND, U2.GND
  N1: DHT11_1.DATA, U2.D2

custom parts:
  DHT11 module: DHT11 black pcb module
  NodeMCU V3.0: ESP8266 based NodeMCU
